# Fritzing sketch verkabelung (saved by Fritzing 0.9.10b)

parts:
  Raspberry_Pi_4 = Raspberry Pi 4B
  NEMA17-04 = Stepper Motor - Bipolar
  A4988_Driver = Pololu A4988 [package=SO16]
  12_V_Power_Supply = Power plug
  Decoupling_capacitor = Electrolytic Capacitor [capacitance=0.1mF voltage=0.1kV package="200 mil [THT, electrolytic]"]
  Stepper_mit_Linearschlitten = Stepper Motor - Bipolar
  A4988_Driver_2 = Pololu A4988 [package=SO16]
  Decoupling_capacitor_2 = Electrolytic Capacitor [capacitance=0.1mF voltage=0.1kV package="200 mil [THT, electrolytic]"]
  ToF_Micro-LIDAR = Adafruit VL6180 Time of Flight Sensor [part_number="Adafruit #3316"]

nets:
  VDD: Raspberry_Pi_4.5V, A4988_Driver.VDD, A4988_Driver_2.VDD, ToF_Micro-LIDAR.VCC
  GND: Raspberry_Pi_4.GND, A4988_Driver.GND#8, A4988_Driver_2.GND#8, ToF_Micro-LIDAR.GND
  N1: Raspberry_Pi_4.GPIO17, A4988_Driver.STEP
  N2: Raspberry_Pi_4.GPIO27, A4988_Driver.DIR
  N3: Raspberry_Pi_4.GPIO6, A4988_Driver_2.STEP
  N4: Raspberry_Pi_4.GPIO13, A4988_Driver_2.DIR
  N5: Raspberry_Pi_4.GPIO16, ToF_Micro-LIDAR.SDA
  N6: Raspberry_Pi_4.GPIO20, ToF_Micro-LIDAR.SCL
  N7: NEMA17-04.A, A4988_Driver.2B
  N8: NEMA17-04.C, A4988_Driver.2A
  N9: NEMA17-04.B, A4988_Driver.1A
  N10: NEMA17-04.D, A4988_Driver.1B
  N11: A4988_Driver.RESET, A4988_Driver.SLEEP
  N12: A4988_Driver.GND#14, 12_V_Power_Supply.GND, Decoupling_capacitor.-, A4988_Driver_2.GND#14, Decoupling_capacitor_2.-
  N13: A4988_Driver.VMOT, 12_V_Power_Supply.VCC, Decoupling_capacitor.+, A4988_Driver_2.VMOT, Decoupling_capacitor_2.+
  N14: Stepper_mit_Linearschlitten.A, A4988_Driver_2.2B
  N15: Stepper_mit_Linearschlitten.C, A4988_Driver_2.2A
  N16: Stepper_mit_Linearschlitten.B, A4988_Driver_2.1A
  N17: Stepper_mit_Linearschlitten.D, A4988_Driver_2.1B
  N18: A4988_Driver_2.RESET, A4988_Driver_2.SLEEP

notes:
  Drehteller

custom parts:
  Adafruit VL6180 Time of Flight Sensor: The VL6180X (sometimes called the VL6180) is a Time of Flight distance sensor like no other you've used! The sensor contains a very tiny laser source, and a matching sensor. The VL6180X can detect the "time of flight", or how long the laser light has taken to bounce back to the sensor. Since it uses a very narrow light source, it is good for determining distance of only the surface directly in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
